# Fritzing sketch standing_desk (saved by Fritzing 0.9.3b)
circuit board: 8.46667cm x 5.64444cm
breadboards: 2

parts:
  Componente1 = Arduino Nano (Rev3.0)
  S2 = Pushbutton [package="[THT]"]
  S3 = Pushbutton [package="[THT]"]
  S4 = Pushbutton [package="[THT]"]
  S5 = Pushbutton [package="[THT]"]
  S6 = Pushbutton [package="[THT]"]
  LED1 = smd LED [color="Red (633nm)" package="0805 [SMD]"]
  R1 = Resistor [tolerance=±5% resistance=220 package=THT]
  L298N1 = L298N DC motor driver
  hc-sr1 = hc-sr04
  M1 = DC Motor  # not connected
  M2 = DC Motor  # not connected

nets:
  GND: Componente1.GND, S2.Pin_3, S2.Pin_4, S3.Pin_3, S3.Pin_4, S4.Pin_3, S4.Pin_4, S5.Pin_3, S5.Pin_4, S6.Pin_3, S6.Pin_4, LED1.cathode, L298N1.GND, hc-sr1.GND
  N1: Componente1.D2, L298N1.IN1
  N2: Componente1.D3, L298N1.IN2
  N3: Componente1.D4, L298N1.IN3
  N4: Componente1.D5, L298N1.IN4
  N5: Componente1.D6, hc-sr1.Echo
  N6: Componente1.D7, hc-sr1.Trig
  N7: Componente1.D8, S6.Pin_1, S6.Pin_2
  N8: Componente1.D9, S5.Pin_1, S5.Pin_2
  N9: Componente1.D10, S4.Pin_1, S4.Pin_2
  N10: Componente1.D11/MOSI, S3.Pin_1, S3.Pin_2
  N11: Componente1.D12/MISO, S2.Pin_1, S2.Pin_2
  5V: Componente1.5V, L298N1.5V, hc-sr1.VCC
  N12: Componente1.D13/SCK, R1.Pin_1
  N13: LED1.anode, R1.Pin_0

notes:
  12V Power Supply
  5V from L298N to Arduino

custom parts:
  L298N DC motor driver: 2x DC motor driver with 78M05 positive voltage regulator (7..35 V) L298N: max 46 V, 2 A Set 5 V Enable jumper to enable 5 V regultor (needed for the L298N) and +5 V output at screw terminal or supply external +5 V at screw terminal Set ENA and/or ENB to +5 V to enable motor permanently or supply ENA and/or ENB with PWM signal IN1 and IN2 set rotation directory for motor A (OUT1/OUT2) IN2 and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
